# Fritzing sketch basiccircuit_led (saved by Fritzing 0.9.3b)
breadboards: 1

parts:
  S1 = Pushbutton [package="[THT]"]
  LED1 = smd LED [color="Red (633nm)" package="0603 [SMD]"]
  VCC1 = Battery
  R1 = Resistor [tolerance=±5% resistance=220 package="2512 [SMD]"]

nets:
  N1: S1.Pin_1, S1.Pin_2, LED1.cathode
  N2: S1.Pin_3, S1.Pin_4, VCC1.-
  N3: LED1.anode, R1.Pin_0
  N4: VCC1.+, R1.Pin_1
