# Fritzing sketch multiple_leds (saved by Fritzing 0.9.3b)
breadboards: 1

parts:
  Part1 = Arduino Uno (Rev3)
  LED1 = smd LED [color="Red (633nm)" package="1206 [SMD]"]
  R1 = Resistor [tolerance=±5% resistance=220 package=THT]
  LED2 = smd LED [color="Red (633nm)" package="1206 [SMD]"]  # not connected
  R2 = Resistor [tolerance=±5% resistance=220 package=THT]

nets:
  N1: Part1.D12/MISO, R2.Pin_0
  N2: Part1.D13/SCK, R1.Pin_0
  N3: Part1.GND, LED1.cathode
  N4: LED1.anode, R1.Pin_1
