# Fritzing sketch noise_monitor (saved by Fritzing 0.9.3b)
breadboards: 1

parts:
  Part1 = Arduino Uno (Rev3)
  LED1 = smd LED [color="Red (633nm)" package="1206 [SMD]"]
  LED3 = smd LED [color="Red (633nm)" package="1206 [SMD]"]  # not connected
  MIC1 = Electret Microphone Amplifier
  R3 = Resistor [tolerance=±5% resistance=220 package=THT]
  R4 = Resistor [tolerance=±5% resistance=220 package=THT]
  R5 = Resistor [tolerance=±5% resistance=220 package=THT]  # not connected
  LED4 = smd LED [color="Red (633nm)" package="1206 [SMD]"]

nets:
  N1: Part1.A5/SCL, MIC1.OUT
  N2: Part1.D12/MISO, R4.Pin_0
  N3: Part1.D13/SCK, R3.Pin_0
  GND: Part1.GND, LED1.cathode, MIC1.GND, LED4.cathode
  3V3: Part1.3V3, MIC1.VDD
  N4: LED1.anode, R3.Pin_1
  N5: R4.Pin_1, LED4.anode

custom parts:
  Electret Microphone Amplifier: Electret Microphone Amplifier - MAX9814 with Auto Gain Control
