# Fritzing sketch grove_light_sensor (saved by Fritzing 0.9.3b)

parts:
  Part1 = Arduino Uno (Rev3)
  Grove1 = Grove Light Sensor

nets:
  N1: Part1.A0, Grove1.SIG
  5V: Part1.5V, Grove1.VCC
  GND: Part1.GND, Grove1.GND
