# Fritzing sketch light_sensor (saved by Fritzing 0.9.3b)

parts:
  Part1 = Photo Sensor with LM393
  Part2 = Arduino Uno (Rev3)

nets:
  GND: Part1.GND, Part2.GND
  VCC: Part1.VCC, Part2.3V3
  N1: Part1.DO, Part2.D3_PWM

custom parts:
  Photo Sensor with LM393: Photo Sensor
