# Fritzing sketch motion_sensor (saved by Fritzing 0.9.3b)

parts:
  Part1 = PIR Motion Sensor
  Part2 = Arduino Uno (Rev3)

nets:
  GND: Part1.GND, Part2.GND
  +5V: Part1.+5V, Part2.5V
  N1: Part1.OUT, Part2.A2

custom parts:
  PIR Motion Sensor: PIR
