# Fritzing sketch joystick (saved by Fritzing 0.9.3b)

parts:
  Part1 = Arduino Uno (Rev3)
  Part2 = Seeed Studio Grove Thumb Joystick

nets:
  N1: Part1.A0, Part2.X
  N2: Part1.A1, Part2.Y
  5V: Part1.5V, Part2.VCC
  GND: Part1.GND, Part2.GND

custom parts:
  Seeed Studio Grove Thumb Joystick: Grove - Thumb Joystick is a Grove compatible module which is very similar to the 'analog' joystick on PS2 (PlayStation 2) controllers. Two direction movements will output different analog signals as they are actually two potentiometers. The resistor is ~10k for each. The joystick also has a push button that is could be used for special applications. When the module is in working mode it will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
