# Fritzing sketch hc-sr04 (saved by Fritzing 0.9.3b)
breadboards: 1

parts:
  Part1 = Arduino Uno (Rev3)
  hc-sr2 = hc-sr04

nets:
  N1: Part1.D11_PWM/MOSI, hc-sr2.Trig
  N2: Part1.D3_PWM, hc-sr2.Echo
  5V: Part1.5V, hc-sr2.VCC
  GND: Part1.GND, hc-sr2.GND
