# Fritzing sketch capacitive_touch_sensor (saved by Fritzing 0.9.3b)

parts:
  Part1 = Arduino Uno (Rev3) - ICSP
  Part2 = MPR121 Adafruit Breakout

nets:
  N1: Part1.A4/SDA, Part2.SDA
  N2: Part1.A5/SCL, Part2.SCL
  5V: Part1.5V, Part2.VIN
  GND: Part1.GND, Part2.GND

custom parts:
  MPR121 Adafruit Breakout: This is a breakout board for Freescale’s MPR121QR2. The MPR121 is a capacitive touch sensor controller driven by an I2C interface. The chip can control up to twelve individual electrodes, as well as a simulated thirteenth electrode. The MPR121 also features eight LED driving pins. When these pins are not configured as electrodes, they may be used to drive LEDs. There a four jumpers on the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
