# Fritzing sketch accelerometer_adxl345 (saved by Fritzing 0.9.3b)
breadboards: 1

parts:
  Part1 = Adafruit ADXL345 [part_number="Adafruit #1231"]
  Part2 = Arduino Uno (Rev3)

nets:
  VIN: Part1.VIN, Part2.5V
  GND: Part1.GND, Part2.GND
  N1: Part1.SDA/SDIO, Part2.A4/SDA
  N2: Part1.SCL, Part2.A5/SCL

custom parts:
  Adafruit ADXL345: Filling out our accelerometer offerings, we now have the really lovely digital ADXL345 from Analog Devices, a triple-axis accelerometer with digital I2C and SPI interface breakout. We added an on-board 3.3V regulator and logic-level shifting circuitry, making it a perfect choice for interfacing with any 3V or 5V microcontroller such as the Arduino. The sensor has three axes of measurements, X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
