# Fritzing sketch arduino_two_dc_motor (saved by Fritzing 0.9.3b)
breadboards: 1

parts:
  Part1 = Arduino Uno (Rev3)
  M1 = DC Motor
  M2 = DC Motor
  VCC1 = 4 x AAA Battery Mount
  IC1 = L293D [package=THT]

nets:
  N1: Part1.D10_PWM/SS, IC1.In_2
  N2: Part1.D11_PWM/MOSI, IC1.In_1
  N3: Part1.D12/MISO, IC1.In_4
  N4: Part1.D13/SCK, IC1.In_3
  N5: Part1.5V, IC1.Enable_1, IC1.+V
  N6: Part1.GND, VCC1.-, IC1.0V
  N7: M1.pin_1, IC1.Out_2_(_Controlled_by_Enable_1_)
  N8: M1.pin_2, IC1.Out_1_(_Controlled_by_Enable_1_)
  N9: M2.pin_1, IC1.Out_4_(_Controlled_by_Enable_2_)
  N10: M2.pin_2, IC1.Out_3_(_Controlled_by_Enable_2_)
  N11: VCC1.+, IC1.+Vmotor
