# Fritzing sketch arduino_two_dc_motor_xbee_hc-sr04 (saved by Fritzing 0.9.3b)
breadboards: 1

parts:
  Part1 = Arduino Uno (Rev3)
  M1 = DC Motor
  M2 = DC Motor
  VCC1 = 4 x AAA Battery Mount
  IC1 = L293D [package=THT]
  U1 = XBee
  hc-sr1 = hc-sr04

nets:
  N1: Part1.D10_PWM/SS, IC1.In_2
  N2: Part1.D11_PWM/MOSI, IC1.In_1
  N3: Part1.D12/MISO, IC1.In_4
  N4: Part1.D13/SCK, IC1.In_3
  N5: Part1.D0/RX, U1.pin2
  N6: Part1.D1/TX, U1.pin3
  N7: Part1.D3_PWM, hc-sr1.Trig
  N8: Part1.D4, hc-sr1.Echo
  3V3: Part1.3V3, U1.VCC
  5V: Part1.5V, IC1.Enable_1, IC1.+V, hc-sr1.VCC
  GND: Part1.GND, U1.GND
  N9: Part1.VIN, VCC1.+, IC1.+Vmotor
  N10: M1.pin_1, IC1.Out_2_(_Controlled_by_Enable_1_)
  N11: M1.pin_2, IC1.Out_1_(_Controlled_by_Enable_1_)
  N12: M2.pin_1, IC1.Out_4_(_Controlled_by_Enable_2_)
  N13: M2.pin_2, IC1.Out_3_(_Controlled_by_Enable_2_)
  N14: VCC1.-, IC1.0V, hc-sr1.GND
